// Logisim project alu.circ as structural Verilog: 1 circuit, main circuit alu
module alu (
  input  [31:0] A,
  input  [31:0] B,
  input  [3:0] ALUSel,
  input  [31:0] in_4,
  input  [31:0] in_5,
  output [31:0] Result,
  output [31:0] out_7,
  output [31:0] out_8,
  output [31:0] out_9,
  output [31:0] out_10,
  output [31:0] out_11,
  output [31:0] out_12
);

  wire comparator_1_lt, slt;
  wire [4:0] bit_extender_1_out, bit_extender_2_out, bit_extender_3_out, bit_extender_4_out,
       bit_extender_5_out, bit_extender_6_out;
  wire [31:0] add, adder_1_out, and1, and_1_out, bit_extender_7_out, divider_1_out, divider_2_out,
       divider_3_out, divu, mulh, mulhu, mult, multiplier_1_out, multiplier_2_out, multiplier_3_out,
       multiplier_4_out, multiplier_5_out, or1, or_1_out, remu, shifter_1_out, shifter_2_out, shifter_3_out,
       sll1, sra1, srl1, sub, subtractor_1_out, subtractor_2_out, xor1, xor_1_out;

  Divider #(.width(32)) divider_1 (.a(A), .b(B), .out(divider_1_out));  // open: upper, rem
  Bit_Extender #(.in_width(32), .out_width(5)) bit_extender_1 (.in(B), .out(bit_extender_1_out));
  Bit_Extender #(.in_width(32), .out_width(5)) bit_extender_2 (.in(B), .out(bit_extender_2_out));
  Bit_Extender #(.in_width(32), .out_width(5)) bit_extender_3 (.in(B), .out(bit_extender_3_out));
  Adder #(.width(32)) adder_1 (.a(A), .b(B), .out(adder_1_out));  // open: cin, cout
  assign and_1_out = A & B;  // AND_Gate and_1, 32 bits wide
  assign or_1_out = A | B;  // OR_Gate or_1, 32 bits wide
  assign xor_1_out = A ^ B;  // XOR_Gate xor_1, 32 bits wide
  Shifter #(.width(32), .shift("lr")) shifter_1 (.in(A), .\dist (bit_extender_4_out), .out(shifter_1_out));
  Bit_Extender #(.in_width(32), .out_width(5)) bit_extender_4 (.in(B), .out(bit_extender_4_out));
  Shifter #(.width(32), .shift("ar")) shifter_2 (.in(A), .\dist (bit_extender_5_out), .out(shifter_2_out));
  Bit_Extender #(.in_width(32), .out_width(5)) bit_extender_5 (.in(B), .out(bit_extender_5_out));
  Shifter #(.width(32)) shifter_3 (.in(A), .\dist (bit_extender_6_out), .out(shifter_3_out));
  Bit_Extender #(.in_width(32), .out_width(5)) bit_extender_6 (.in(B), .out(bit_extender_6_out));
  Comparator #(.width(32)) comparator_1 (.a(A), .b(B), .lt(comparator_1_lt));  // open: gt, eq
  Divider #(.width(32)) divider_2 (.a(A), .b(B), .out(divider_2_out));  // open: upper, rem
  Multiplier #(.width(32)) multiplier_1 (.a(divider_1_out), .b(B), .out(multiplier_1_out));  // open: cin, cout
  Multiplier #(.width(32)) multiplier_2 (.a(A), .b(B), .out(multiplier_2_out));  // open: cin, cout
  Multiplier #(.width(32)) multiplier_3 (.a(A), .b(B), .out(multiplier_3_out));  // open: cin, cout
  Subtractor #(.width(32)) subtractor_1 (.a(A), .b(B), .out(subtractor_1_out));  // open: bin, bout
  Multiplier #(.width(32)) multiplier_4 (.a(A), .b(B), .out(multiplier_4_out));  // open: cin, cout
  Adder #(.width(32)) adder_2 (.a(A), .b(B), .out(add));  // open: cin, cout
  assign and1 = A & B;  // AND_Gate and_2, 32 bits wide
  assign or1 = A | B;  // OR_Gate or_2, 32 bits wide
  assign xor1 = A ^ B;  // XOR_Gate xor_2, 32 bits wide
  Shifter #(.width(32), .shift("lr")) shifter_4 (.in(A), .\dist (bit_extender_1_out), .out(srl1));
  Shifter #(.width(32), .shift("ar")) shifter_5 (.in(A), .\dist (bit_extender_2_out), .out(sra1));
  Shifter #(.width(32)) shifter_6 (.in(A), .\dist (bit_extender_3_out), .out(sll1));
  assign bit_extender_7_out = {{31{comparator_1_lt}}, comparator_1_lt};  // Bit_Extender bit_extender_7
  Subtractor #(.width(32)) subtractor_2 (.a(A), .b(multiplier_1_out), .out(subtractor_2_out));  // open: bin, bout
  Divider #(.width(32)) divider_3 (.a(A), .b(B), .out(divider_3_out));  // open: upper, rem
  Comparator #(.width(32)) comparator_2 (.a(A), .b(B), .lt(slt));  // open: gt, eq
  Divider #(.width(32)) divider_4 (.a(A), .b(B), .out(divu));  // open: upper, rem
  Multiplier #(.width(32)) multiplier_5 (.a(divider_3_out), .b(B), .out(multiplier_5_out));  // open: cin, cout
  Multiplier #(.width(32)) multiplier_6 (.a(A), .b(B), .out(mult));  // open: cin, cout
  Multiplier #(.width(32)) multiplier_7 (.a(A), .b(B), .out(mulh));  // open: cin, cout
  Multiplier #(.width(32)) multiplier_8 (.a(A), .b(B), .out(mulhu));  // open: cin, cout
  Subtractor #(.width(32)) subtractor_3 (.a(A), .b(B), .out(sub));  // open: bin, bout
  Multiplexer #(.select(4), .width(32), .enable("false")) multiplexer_1 (
    .in0(adder_1_out), .in1(and_1_out), .in2(or_1_out), .in3(xor_1_out), .in4(shifter_1_out),
    .in5(shifter_2_out), .in6(shifter_3_out), .in7(bit_extender_7_out), .in8(divider_2_out),
    .in9(subtractor_2_out), .in10(multiplier_2_out), .in11(multiplier_3_out), .in12(subtractor_1_out),
    .in13(B), .in14(multiplier_4_out), .out(Result), .sel(ALUSel));  // open: in15
  Subtractor #(.width(32)) subtractor_4 (.a(A), .b(multiplier_5_out), .out(remu));  // open: bin, bout
  Multiplier #(.width(32)) multiplier_9 (.a(in_4), .b(in_5), .out(out_7), .cout(out_10));  // open: cin

  assign out_8 = in_4;
  assign out_9 = out_7;
  assign out_11 = out_10;
  assign out_12 = in_5;

  // Other names for the same wires on the sheet: bsel[31:0] = B

  // Notes on the sheet:
  //   INPUTS to your circuit
  //   DON'T CHANGE THE LOCATIONS OF THE INPUTS AND OUTPUTS!
  //   OUTPUT from your circuit
endmodule
